# Fritzing sketch diagrama_control_is_an_illusion (saved by Fritzing 0.8.7b)
breadboards: 1

parts:
  U1 = LCD-16X2 [package=lcd-16x2]
  U2 = POT [package=pot_alpha_rv16af-20]
  Componente4 = IR Receiver Breakout [package=PCB]
  Componente3 = Thumb Joystick
  Componente1 = Arduino Uno (Rev3)
  Componente2 = Thumb Joystick

nets:
  GND: U1.VSS, U1.R_W, U1.K, U2.E, Componente4.GND, Componente3.VERT, Componente1.GND, Componente2.VERT
  VCC: U1.VDD, U1.A, U2.A, Componente4.OUT, Componente3.VCC, Componente1.5V, Componente2.VCC
  N1: U1.VO, U2.S
  N2: U1.RS, Componente1.D8
  N3: U1.E, Componente1.D9_PWM
  N4: U1.DB4, Componente1.D10_PWM/SS
  N5: U1.DB5, Componente1.D11_PWM/MOSI
  N6: U1.DB6, Componente1.D12/MISO
  N7: U1.DB7, Componente1.D13/SCK
  N8: Componente4.VCC, Componente1.D2
  N9: Componente3.GND, Componente1.D3_PWM
  N10: Componente3.SEL, Componente1.A2
  N11: Componente3.HORZ, Componente1.A3
  N12: Componente1.A0, Componente2.SEL
  N13: Componente1.A1, Componente2.HORZ
  N14: Componente1.D4, Componente2.GND
